# Fritzing sketch client_station (saved by Fritzing 0.9.3b)
breadboards: 1

parts:
  Part2 = Photon
  Button = Pushbutton [package="[THT]"]
  LED = LED - 5mm [color="Red (633nm)" package="5 mm [THT]"]

nets:
  N1: Part2.GND, Button.Pin_1, Button.Pin_2, LED.cathode
  N2: Part2.D0, Button.Pin_3, Button.Pin_4
  N3: Part2.D1, LED.anode
