# Fritzing sketch master_station (saved by Fritzing 0.9.3b)
breadboards: 1

parts:
  part = Photon
  part_2 = 7-Segment LED Display [package=THT]
  part_3 = 7-Segment LED Display [package=THT]

nets:
  N1: part.A0, part_2.cathodeE
  N2: part.A1, part_2.cathodeD
  N3: part.A2, part_2.cathodeC
  N4: part.A3, part_3.cathodeE
  N5: part.A4, part_3.cathodeD
  N6: part.A5, part_3.cathodeC
  N7: part.GND, part_2.commAnode, part_3.commAnode
  N8: part.D0, part_2.cathodeG
  N9: part.D1, part_2.cathodeF
  N10: part.D2, part_2.cathodeA
  N11: part.D3, part_2.cathodeB
  N12: part.D4, part_3.cathodeG
  N13: part.D5, part_3.cathodeF
  N14: part.D6, part_3.cathodeA
  N15: part.D7, part_3.cathodeB
